# Fritzing sketch Home Automation Circuit Diagram (saved by Fritzing 0.8.7b)

parts:
  U1 = ESP32-38PinWide [part_number=ESP32-38PinWide]
  DHT1 = DHT11 Humitidy and Temperature Sensor
  KY-1 = Keyes Relay [package=THT]
  KY-2 = Keyes Relay [package=THT]
  FC-1 = Sound Sensor
  KY-3 = Keyes Relay [package=THT]

nets:
  VDD: U1.3.3, DHT1.VDD, KY-1.power, KY-2.power, FC-1.VCC, KY-3.power
  GND: U1.GND, DHT1.GND, KY-1.ground, KY-2.ground, FC-1.GND, KY-3.ground
  N1: U1.GPIO13, KY-2.signal
  N2: U1.GPIO8, FC-1.OUT
  N3: U1.GPIO2, DHT1.DATA
  N4: U1.GPIO4, KY-1.signal
  N5: U1.GPIO18, KY-3.signal

notes:
  Fan Relay
  Light Relay
  Disco Light Relay

custom parts:
  ESP32-38PinWide: Generic 38-Pin ESP32 with wide format (only access to one side of pins on a breadboard) based on Stephen Lilley's HiLetgo ESP-WROOM-32 ESP32 ESP-32S Development Board.
  DHT11 Humitidy and Temperature Sensor: DHT11 Humidity and Temperature Sensor
  Keyes Relay: The Keyes 5V relay module is suitable for SCM development, home appliance control. It uses a 5V~12V TIL control signal which can control DC / AC signal.
